# Fritzing sketch rainbow_tail_light_circuit (saved by Fritzing 0.9.3b)

parts:
  Part1 = Arduino Pro Micro (Clone)
  S1 = Toggle Switch [package=THT]
  SparkFun_LiPo_Charger_Basic_-_Micro-USB1 = SparkFun LiPo Charger Basic - Micro-USB [part_number=PRT-10217]
  Part2 = 12 NeoPixel Ring [part_number=1643]
  U1 = LIPO-110mAh [package=lipo-110]

nets:
  GND: Part1.GND, SparkFun_LiPo_Charger_Basic_-_Micro-USB1.GND, Part2.GND, U1.-
  N1: Part1.D2, Part2.IN
  VCC: Part1.VCC, Part2.VDD
  N2: Part1.RAW, S1.L2
  N3: S1.COM, SparkFun_LiPo_Charger_Basic_-_Micro-USB1.VCC, U1.+

notes:
  400mAh 3.7v
  Should actually have 8 LEDs

custom parts:
  SparkFun LiPo Charger Basic - Micro-USB: Description: If you need to charge LiPo batteries, this simple charger will do just that, and do it fast! The SparkFun LiPo Charger Basic is stripped down of all features and just does one thing well - charge 3.7V LiPo cells at a rate of 500mA. It is designed to charge single-cell Li-Ion or Li-Polymer batteries. Check the datasheet below to see if it will work with your battery. The board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
  12 NeoPixel Ring: 12 ultra bright smart LED NeoPixels are arranged in a circle with 1.5" (37mm) outer diameter. The rings are 'chainable' - connect the output pin of one to the input pin of another. Use only one microcontroller pin to control as many as you can chain together! Each LED is addressable as the driver chip is inside the LED. Each one has ~18mA constant current drive so the color will be very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
